# Fritzing sketch soil-moisture-system-schema (saved by Fritzing 0.9.3b)

parts:
  Součástka10 = FC-28 Soil Hygrometer Module
  Součástka12 = FC-28 Soil Hygrometer Module
  Součástka13 = FC-28 Soil Hygrometer Module
  Součástka14 = FC-28 Soil Hygrometer Module
  Součástka15 = FC-28 Soil Hygrometer Module
  MUX2 = 74HC4051 [package="DIP (Dual Inline) [THT]"]
  WeMos_D1_Mini2 = WeMos D1 Mini
  Součástka16 = FC-28 Soil Hygrometer Module
  Součástka17 = FC-28 Soil Hygrometer Module
  Q1 = Basic FET N-Channel [package="TO220 [THT]"]

nets:
  VCC: Součástka10.VCC, Součástka12.VCC, Součástka13.VCC, Součástka14.VCC, Součástka15.VCC, MUX2.VDD, WeMos_D1_Mini2.3V3, Součástka16.VCC, Součástka17.VCC
  GND: Součástka10.GND, Součástka12.GND, Součástka13.GND, Součástka14.GND, Součástka15.GND, Součástka16.GND, Součástka17.GND, Q1.drain
  N1: Součástka10.AO, MUX2.IO4
  N2: Součástka12.AO, MUX2.IO1
  N3: Součástka13.AO, MUX2.IO0
  N4: Součástka14.AO, MUX2.IO3
  N5: Součástka15.AO, MUX2.IO2
  N6: MUX2.IO6, Součástka17.AO
  N7: MUX2.IO, WeMos_D1_Mini2.A0
  N8: MUX2.IO5, Součástka16.AO
  N9: MUX2.INH, MUX2.VEE, MUX2.VSS, WeMos_D1_Mini2.G, Q1.source
  N10: MUX2.C, WeMos_D1_Mini2.D6
  N11: MUX2.B, WeMos_D1_Mini2.D5
  N12: MUX2.A, WeMos_D1_Mini2.D0
  N13: WeMos_D1_Mini2.D3, Q1.gate

custom parts:
  FC-28 Soil Hygrometer Module: The FC-28 is a soil hygrometer module that uses the Texas Instruments LM393 comparator chip to provide an analog measurement of soil humidity. The digital output is high when soil moisture is over a certain threshold, as determined by adjusting the potentiometer.
  74HC4051: 8 channel analog multiplexer/demultiplexer
